# Fritzing sketch Halloween_2017_Contest (saved by Fritzing 0.9.3b)
breadboards: 1

parts:
  Componente1 = Arduino Nano (Rev3.0)
  J1 = Piezo Speaker
  J2 = Infrared Proximity Sensor
  LCD1 = LCD screen
  Part1 = Serial Enabled LCD Backpack [part_number=LCD-00258]
  Componente2 = 12 NeoPixel Ring [part_number=1643]
  Componente3 = 12 NeoPixel Ring [part_number=1643]

nets:
  GND: Componente1.GND, J1.pin1, J2.GND, LCD1.V0, Part1.GND, Componente2.GND
  N1: Componente1.D2, J2.Vout
  N2: Componente1.D4, Componente3.IN
  N3: Componente1.D6, Part1.RX
  N4: Componente1.D8, J1.pin2
  N5: Componente1.D9, Componente2.IN
  5V: Componente1.5V, J2.Vcc, LCD1.VSS, Part1.5V, Componente3.VDD
  N6: LCD1.DB4, Part1.D4
  N7: LCD1.DB5, Part1.D5
  N8: LCD1.DB6, Part1.D6
  N9: LCD1.DB7, Part1.D7

custom parts:
  Serial Enabled LCD Backpack: The serial enabled LCD backpack allows you to control a parallel based LCD over a single-wire serial interface. The SerLCD backpack takes care of all the HD44780 commands allowing seamless integration with any micro that can communicate over a wide range of TTL serial baud rates. The SerLCD currently supports 16 and 20 character wide screens with 2 or 4 lines of display. Communication with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
  12 NeoPixel Ring: 12 ultra bright smart LED NeoPixels are arranged in a circle with 1.5" (37mm) outer diameter. The rings are 'chainable' - connect the output pin of one to the input pin of another. Use only one microcontroller pin to control as many as you can chain together! Each LED is addressable as the driver chip is inside the LED. Each one has ~18mA constant current drive so the color will be very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
